# Fritzing sketch pico-car (saved by Fritzing 0.9.3b)
breadboards: 1

parts:
  L298N1 = L298N DC motor driver
  S1 = Toggle Switch spst [package=THT]
  M2 = DC Motor  # not connected
  M3 = DC Motor  # not connected
  VCC1 = 4 x AAA Battery Mount
  Part1 = GY-VL53L0XV2 Laser Ranger Module
  Part2 = GY-VL53L0XV2 Laser Ranger Module
  Mod1 = Raspberry Pi Pico W
  Part3 = Adafruit BNO085 9-DOF Orientation IMU Fusion [part_number="Addfruit #4754"]

nets:
  N1: L298N1.12V, S1.COM
  GND: L298N1.GND, VCC1.-, Part1.GND, Part2.GND, Mod1.pin_3, Mod1.pin_8, Mod1.pin_13, Mod1.pin_18, Mod1.pin_23, Mod1.pin_28, Mod1.pin_33, Mod1.pin_38, Part3.GND
  N2: L298N1.5V, Mod1.pin_39
  N3: L298N1.ENA, Mod1.pin_27
  N4: L298N1.ENB, Mod1.pin_21
  N5: L298N1.IN1, Mod1.pin_26
  N6: L298N1.IN2, Mod1.pin_25
  N7: L298N1.IN3, Mod1.pin_24
  N8: L298N1.IN4, Mod1.pin_22
  N9: S1.L1, VCC1.+
  VCC: Part1.VCC, Part1.XSHUT, Part2.VCC, Part2.XSHUT, Mod1.pin_36, Part3.VCC
  N10: Part1.SCL, Mod1.pin_17
  N11: Part1.SDA, Mod1.pin_16
  N12: Part2.SCL, Mod1.pin_20
  N13: Part2.SDA, Mod1.pin_19
  N14: Mod1.pin_1, Part3.SCL/SCK/RX
  N15: Mod1.pin_2, Part3.SDA/MISO/TX

notes:
  5V
  3V3
  6V

custom parts:
  L298N DC motor driver: 2x DC motor driver with 78M05 positive voltage regulator (7..35 V) L298N: max 46 V, 2 A Set 5 V Enable jumper to enable 5 V regultor (needed for the L298N) and +5 V output at screw terminal or supply external +5 V at screw terminal Set ENA and/or ENB to +5 V to enable motor permanently or supply ENA and/or ENB with PWM signal IN1 and IN2 set rotation directory for motor A (OUT1/OUT2) IN2 and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
  Toggle Switch spst: Toggle Switch single pole single throw
  GY-VL53L0XV2 Laser Ranger Module: The GY-VL53L0XV2 is based on the VL53L0X from ST Microelectronics, a time-of-flight ranging system integrated into a compact module.
  Raspberry Pi Pico W: Raspberry Pi Pico W. Based around the RP2040 microcontroller the Pico W is a low cost microcontroller device bringing Raspberry Pi quality, cost, and easy of use to the microcontroller space. The areas marked KEEPOUT in pcb silkscreen should not have traces running through them to avoid shorts on a soldered in module!
