# Fritzing sketch pico-car2 (saved by Fritzing 0.9.3b)
breadboards: 1

parts:
  L298N1 = L298N DC motor driver
  IC1 = IC, SIP package, 6 pins
  IC2 = IC, SIP package, 6 pins
  M1 = Stepper Motor - Bipolar  # not connected
  M2 = Stepper Motor - Bipolar  # not connected
  Mod1 = Raspberry Pi Pico W
  D1 = Rectifier Diode [part_number=1N5817 package="300 mil [THT]"]
  BATT1 = LiPoly Battery (1300mAh)
  S1 = Toggle Switch spst [package=THT]

nets:
  N1: L298N1.OUT1, IC2.pin6
  N2: L298N1.OUT2, IC2.pin1
  N3: L298N1.OUT3, IC1.pin6
  N4: L298N1.OUT4, IC1.pin1
  N5: L298N1.12V, S1.L1
  N6: L298N1.GND, IC1.pin2, IC2.pin2, Mod1.pin_3, Mod1.pin_8, Mod1.pin_13, Mod1.pin_18, Mod1.pin_23, Mod1.pin_28, Mod1.pin_33, Mod1.pin_38, BATT1.negative
  N7: L298N1.5V, IC1.pin5
  N8: L298N1.ENA, Mod1.pin_27
  N9: L298N1.ENB, Mod1.pin_21
  N10: L298N1.IN1, Mod1.pin_26
  N11: L298N1.IN2, Mod1.pin_25
  N12: L298N1.IN3, Mod1.pin_24
  N13: L298N1.IN4, Mod1.pin_22
  N14: IC1.pin3, Mod1.pin_16
  N15: IC1.pin4, Mod1.pin_17
  N16: IC2.pin3, Mod1.pin_20
  N17: IC2.pin4, Mod1.pin_19
  N18: IC2.pin5, D1.anode
  N19: Mod1.pin_39, D1.cathode
  N20: BATT1.positive, S1.COM

custom parts:
  L298N DC motor driver: 2x DC motor driver with 78M05 positive voltage regulator (7..35 V) L298N: max 46 V, 2 A Set 5 V Enable jumper to enable 5 V regultor (needed for the L298N) and +5 V output at screw terminal or supply external +5 V at screw terminal Set ENA and/or ENB to +5 V to enable motor permanently or supply ENA and/or ENB with PWM signal IN1 and IN2 set rotation directory for motor A (OUT1/OUT2) IN2 and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
  Raspberry Pi Pico W: Raspberry Pi Pico W. Based around the RP2040 microcontroller the Pico W is a low cost microcontroller device bringing Raspberry Pi quality, cost, and easy of use to the microcontroller space. The areas marked KEEPOUT in pcb silkscreen should not have traces running through them to avoid shorts on a soldered in module!
  LiPoly Battery (1300mAh): Lithium Ion Polymer Battery (1300mAh)
  Toggle Switch spst: Toggle Switch single pole single throw
